# Fritzing sketch PiAudioButton (saved by Fritzing 0.9.3b)
breadboards: 1

parts:
  Raspberry_Pi_1 = Raspberry Pi 3 [part_number=RPI-3-V1.2]
  S1 = Pushbutton [package="[THT]"]
  S2 = Pushbutton [package="[THT]"]
  Part1 = Adafruit Stereo 2.1W Class D Audio Amplifier - TPA2012 [part_number="Adafruit #1552"]
  SP1 = SPEAKER [package=pcb_mount_speaker]
  TRS1 = Audio Jack (TRS) 3.5mm [package="PG203J [THT]"]

nets:
  GND: Raspberry_Pi_1.GND, S1.Pin_3, S1.Pin_4, S2.Pin_1, S2.Pin_2, Part1.GND
  N1: Raspberry_Pi_1.GPIO17, S1.Pin_1, S1.Pin_2
  N2: Raspberry_Pi_1.GPIO21, S2.Pin_3, S2.Pin_4
  5V: Raspberry_Pi_1.5V, Part1.VDD
  N3: Part1.OUT_RIGHT+, SP1.+
  N4: Part1.OUT_RIGHT-, SP1.-
  N5: Part1.IN_RIGHT+, Part1.IN_RIGHT-, TRS1.Ring
  N6: Part1.IN_LEFT-, Part1.IN_LEFT+, TRS1.Tip

custom parts:
  Adafruit Stereo 2.1W Class D Audio Amplifier - TPA2012: This incredibly small stereo amplifier is surprisingly powerful - able to deliver 2 x 2.1W channels into 4 ohm impedance speakers (@ 10% THD). Inside the miniature chip is a class D controller, able to run from 2.7V-5.5VDC. Since the amp is a class D, it's incredibly efficient (89% efficient when driving an 8Ω speaker at 1.5 Watt) - making it perfect for portable and battery-powered projects.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
